// Digital circuit MUX4X1_BUS.dig as structural Verilog
module MUX4X1_BUS (
  input  [3:0] a,
  input  [3:0] b,
  input  [3:0] c,
  input  [3:0] d,
  input  [3:0] e,
  input  [3:0] f,
  input  x1,
  input  s2,
  input  s1,
  input  s0,
  output [3:0] Dino
);

  cmux_core cmux_core_1 (
    .a(a[3]), .b(b[3]), .c(c[3]), .d(d[3]), .e(e[3]), .f(f[3]), .s2(s2), .s1(s1), .s0(s0), .x1(x1),
    .din(Dino[3]));
  cmux_core cmux_core_2 (
    .a(a[2]), .b(b[2]), .c(c[2]), .d(d[2]), .e(e[2]), .f(f[2]), .s2(s2), .s1(s1), .s0(s0), .x1(x1),
    .din(Dino[2]));
  cmux_core cmux_core_3 (
    .a(a[1]), .b(b[1]), .c(c[1]), .d(d[1]), .e(e[1]), .f(f[1]), .s2(s2), .s1(s1), .s0(s0), .x1(x1),
    .din(Dino[1]));
  cmux_core cmux_core_4 (
    .a(a[0]), .b(b[0]), .c(c[0]), .d(d[0]), .e(e[0]), .f(f[0]), .s2(s2), .s1(s1), .s0(s0), .x1(x1),
    .din(Dino[0]));
endmodule
