// Digital circuit VoteComparator.dig as structural Verilog
module VoteComparator (
  input  [15:0] main,
  input  [15:0] com__2,
  input  [15:0] com__3,
  input  [15:0] com__4,
  input  [15:0] com__1,
  input  votes__done,
  output winner
);

  wire and_1_out, comparator_1_gt, comparator_2_gt, comparator_3_gt, comparator_4_gt;

  Comparator #(.Bits(16)) comparator_1 (.a(main), .b(com__1), .gt(comparator_1_gt));  // open: eq, lt
  Comparator #(.Bits(16)) comparator_2 (.a(main), .b(com__2), .gt(comparator_2_gt));  // open: eq, lt
  Comparator #(.Bits(16)) comparator_3 (.a(main), .b(com__3), .gt(comparator_3_gt));  // open: eq, lt
  Comparator #(.Bits(16)) comparator_4 (.a(main), .b(com__4), .gt(comparator_4_gt));  // open: eq, lt
  and and_1 (and_1_out, comparator_1_gt, comparator_2_gt, comparator_3_gt, comparator_4_gt);
  and and_2 (winner, votes__done, and_1_out);
endmodule
