// Digital circuit VoteCounter.dig as structural Verilog
module VoteCounter (
  input  vote__in,
  output [3:0] _1s,
  output [3:0] _10s,
  output [3:0] _100s,
  output [3:0] _1000s
);

  wire HUNDREDS_ovf, ONES_ovf, TENS_ovf;

  CounterPreset #(.maxValue(9), .Bits(4)) ONES (
    .en(1'b1), .C(vote__in), .dir(1'b0), .in(4'b0000), .ld(1'b0), .clr(1'b0), .out(_1s), .ovf(ONES_ovf));
  CounterPreset #(.maxValue(9), .Bits(4)) TENS (
    .en(ONES_ovf), .C(vote__in), .dir(1'b0), .in(4'b0000), .ld(1'b0), .clr(1'b0), .out(_10s), .ovf(TENS_ovf));
  CounterPreset #(.maxValue(9), .Bits(4)) HUNDREDS (
    .en(TENS_ovf), .C(vote__in), .dir(1'b0), .in(4'b0000), .ld(1'b0), .clr(1'b0), .out(_100s),
    .ovf(HUNDREDS_ovf));
  CounterPreset #(.maxValue(9), .Bits(4)) THOUSANDS (
    .en(HUNDREDS_ovf), .C(vote__in), .dir(1'b0), .in(4'b0000), .ld(1'b0), .clr(1'b0), .out(_1000s));  // open: ovf
endmodule
