// Digital circuit cmux_core.dig as structural Verilog
module cmux_core (
  input  a,
  input  b,
  input  c,
  input  d,
  input  e,
  input  f,
  input  s2,
  input  s1,
  input  s0,
  input  x1,
  output din
);

  wire and_1_out, and_2_out, and_3_out, and_4_out, and_5_out, and_6_out, not_1_out, not_2_out, not_3_out;

  not not_1 (not_1_out, s2);
  not not_2 (not_2_out, s1);
  not not_3 (not_3_out, s0);
  and and_1 (and_1_out, a, not_3_out, not_2_out, not_1_out, x1);
  and and_2 (and_2_out, b, s0, not_2_out, not_1_out, x1);
  and and_3 (and_3_out, c, not_3_out, s1, not_1_out, x1);
  and and_4 (and_4_out, d, s0, s1, not_1_out, x1);
  and and_5 (and_5_out, e, not_3_out, not_2_out, s2, x1);
  and and_6 (and_6_out, f, s0, not_2_out, s2, x1);
  or or_1 (din, and_1_out, and_2_out, and_3_out, and_4_out, and_5_out, and_6_out);
endmodule
