// Digital circuit vote_lock.dig as structural Verilog
module vote_lock (
  input  set,
  input  reset,
  output lock
);

  wire nor_1_out;

  nor nor_1 (nor_1_out, set, lock);
  nor nor_2 (lock, nor_1_out, reset);
endmodule
