// Digital circuit voting_machine.dig as structural Verilog
module voting_machine (
  input  Votes__done,
  input  clk,
  input  [2:0] Select
);

  wire A_out, and_1_out, and_2_out, and_3_out, and_4_out, and_5_out, and_6_out, and_7_out, and_8_out,
       and_9_out, and_10_out, and_11_out, and_12_out, B_out, C_out, d_ff_1_nq, d_ff_2_nq, d_ff_3_nq,
       d_ff_4_nq, d_ff_5_nq, D_out, E_out, N_out, not_1_out, not_2_out, not_3_out, not_4_out, not_5_out,
       not_6_out, not_7_out, or_1_out, vote_lock_1_lock, votecomparator_1_winner, votecomparator_2_winner,
       votecomparator_3_winner, votecomparator_4_winner, votecomparator_5_winner;
  wire [3:0] HUNDREDS_dino, ONES_dino, TENS_dino, THOUSANDS_dino, Total__1s, Total__10s, Total__100s,
       Total__1000s, votecounter_2__1s, votecounter_2__10s, votecounter_2__100s, votecounter_2__1000s,
       votecounter_3__1s, votecounter_3__10s, votecounter_3__100s, votecounter_3__1000s, votecounter_4__1s,
       votecounter_4__10s, votecounter_4__100s, votecounter_4__1000s, votecounter_5__1s, votecounter_5__10s,
       votecounter_5__100s, votecounter_5__1000s;
  wire [15:0] eepromdualport_1_d, votecounter_1__1s;

  Button N (.out(N_out));
  Button A (.out(A_out));
  Button B (.out(B_out));
  Button C (.out(C_out));
  Button D (.out(D_out));
  Button E (.out(E_out));
  not not_1 (not_1_out, Votes__done);
  D_FF d_ff_1 (.D(A_out), .C(A_out), .nQ(d_ff_1_nq));  // open: Q
  D_FF d_ff_2 (.D(B_out), .C(B_out), .nQ(d_ff_2_nq));  // open: Q
  D_FF d_ff_3 (.D(C_out), .C(C_out), .nQ(d_ff_3_nq));  // open: Q
  D_FF d_ff_4 (.D(D_out), .C(D_out), .nQ(d_ff_4_nq));  // open: Q
  D_FF d_ff_5 (.D(E_out), .C(E_out), .nQ(d_ff_5_nq));  // open: Q
  not not_2 (not_2_out, d_ff_1_nq);
  not not_3 (not_3_out, d_ff_2_nq);
  not not_4 (not_4_out, d_ff_3_nq);
  not not_5 (not_5_out, d_ff_4_nq);
  not not_6 (not_6_out, d_ff_5_nq);
  and and_1 (and_1_out, not_2_out, A_out);
  and and_2 (and_2_out, not_3_out, B_out);
  and and_3 (and_3_out, not_4_out, C_out);
  and and_4 (and_4_out, not_5_out, D_out);
  and and_5 (and_5_out, not_6_out, E_out);
  and and_6 (and_6_out, N_out, not_1_out);
  or or_1 (or_1_out, and_1_out, and_2_out, and_3_out, and_4_out, and_5_out);
  vote_lock vote_lock_1 (.set(or_1_out), .reset(and_6_out), .lock(vote_lock_1_lock));
  not not_7 (not_7_out, vote_lock_1_lock);
  LED led_1 (.in(not_7_out));
  and and_7 (and_7_out, or_1_out, not_7_out);
  and and_8 (and_8_out, and_1_out, not_7_out);
  and and_9 (and_9_out, and_2_out, not_7_out);
  and and_10 (and_10_out, and_3_out, not_7_out);
  and and_11 (and_11_out, and_4_out, not_7_out);
  and and_12 (and_12_out, and_5_out, not_7_out);
  VoteCounter Total (
    .vote__in(and_7_out), ._1s(Total__1s), ._10s(Total__10s), ._100s(Total__100s), ._1000s(Total__1000s));
  VoteCounter votecounter_1 (
    .vote__in(and_8_out), ._1s(votecounter_1__1s[3:0]), ._10s(votecounter_1__1s[7:4]),
    ._100s(votecounter_1__1s[11:8]), ._1000s(votecounter_1__1s[15:12]));
  VoteCounter votecounter_2 (
    .vote__in(and_9_out), ._1s(votecounter_2__1s), ._10s(votecounter_2__10s), ._100s(votecounter_2__100s),
    ._1000s(votecounter_2__1000s));
  VoteCounter votecounter_3 (
    .vote__in(and_10_out), ._1s(votecounter_3__1s), ._10s(votecounter_3__10s), ._100s(votecounter_3__100s),
    ._1000s(votecounter_3__1000s));
  VoteCounter votecounter_4 (
    .vote__in(and_11_out), ._1s(votecounter_4__1s), ._10s(votecounter_4__10s), ._100s(votecounter_4__100s),
    ._1000s(votecounter_4__1000s));
  VoteCounter votecounter_5 (
    .vote__in(and_12_out), ._1s(votecounter_5__1s), ._10s(votecounter_5__10s), ._100s(votecounter_5__100s),
    ._1000s(votecounter_5__1000s));
  Seven_Seg_Hex seven_seg_hex_1 (.d(Total__1000s), .dp(1'b0));
  Seven_Seg_Hex seven_seg_hex_2 (.d(Total__100s), .dp(1'b0));
  Seven_Seg_Hex seven_seg_hex_3 (.d(Total__10s), .dp(1'b0));
  Seven_Seg_Hex seven_seg_hex_4 (.d(Total__1s), .dp(1'b0));
  MUX4X1_BUS ONES (
    .a(Total__1s), .b(votecounter_1__1s[3:0]), .c(votecounter_2__1s), .d(votecounter_3__1s),
    .e(votecounter_4__1s), .f(votecounter_5__1s), .x1(1'b1), .s2(Select[2]), .s1(Select[1]), .s0(Select[0]),
    .Dino(ONES_dino));
  MUX4X1_BUS TENS (
    .a(Total__10s), .b(votecounter_1__1s[7:4]), .c(votecounter_2__10s), .d(votecounter_3__10s),
    .e(votecounter_4__10s), .f(votecounter_5__10s), .x1(1'b1), .s2(Select[2]), .s1(Select[1]),
    .s0(Select[0]), .Dino(TENS_dino));
  MUX4X1_BUS HUNDREDS (
    .a(Total__100s), .b(votecounter_1__1s[11:8]), .c(votecounter_2__100s), .d(votecounter_3__100s),
    .e(votecounter_4__100s), .f(votecounter_5__100s), .x1(1'b1), .s2(Select[2]), .s1(Select[1]),
    .s0(Select[0]), .Dino(HUNDREDS_dino));
  MUX4X1_BUS THOUSANDS (
    .a(Total__1000s), .b(votecounter_1__1s[15:12]), .c(votecounter_2__1000s), .d(votecounter_3__1000s),
    .e(votecounter_4__1000s), .f(votecounter_5__1000s), .x1(1'b1), .s2(Select[2]), .s1(Select[1]),
    .s0(Select[0]), .Dino(THOUSANDS_dino));
  VoteComparator votecomparator_1 (
    .main(votecounter_1__1s),
    .com__2({votecounter_2__1000s, votecounter_2__100s, votecounter_2__10s, votecounter_2__1s}),
    .com__3({votecounter_3__1000s, votecounter_3__100s, votecounter_3__10s, votecounter_3__1s}),
    .com__4({votecounter_4__1000s, votecounter_4__100s, votecounter_4__10s, votecounter_4__1s}),
    .com__1({votecounter_5__1000s, votecounter_5__100s, votecounter_5__10s, votecounter_5__1s}),
    .votes__done(Votes__done), .winner(votecomparator_1_winner));
  VoteComparator votecomparator_2 (
    .main({votecounter_2__1000s, votecounter_2__100s, votecounter_2__10s, votecounter_2__1s}),
    .com__2(votecounter_1__1s),
    .com__3({votecounter_3__1000s, votecounter_3__100s, votecounter_3__10s, votecounter_3__1s}),
    .com__4({votecounter_4__1000s, votecounter_4__100s, votecounter_4__10s, votecounter_4__1s}),
    .com__1({votecounter_5__1000s, votecounter_5__100s, votecounter_5__10s, votecounter_5__1s}),
    .votes__done(Votes__done), .winner(votecomparator_2_winner));
  VoteComparator votecomparator_3 (
    .main({votecounter_3__1000s, votecounter_3__100s, votecounter_3__10s, votecounter_3__1s}),
    .com__2(votecounter_1__1s),
    .com__3({votecounter_2__1000s, votecounter_2__100s, votecounter_2__10s, votecounter_2__1s}),
    .com__4({votecounter_4__1000s, votecounter_4__100s, votecounter_4__10s, votecounter_4__1s}),
    .com__1({votecounter_5__1000s, votecounter_5__100s, votecounter_5__10s, votecounter_5__1s}),
    .votes__done(Votes__done), .winner(votecomparator_3_winner));
  VoteComparator votecomparator_4 (
    .main({votecounter_4__1000s, votecounter_4__100s, votecounter_4__10s, votecounter_4__1s}),
    .com__2(votecounter_1__1s),
    .com__3({votecounter_2__1000s, votecounter_2__100s, votecounter_2__10s, votecounter_2__1s}),
    .com__4({votecounter_3__1000s, votecounter_3__100s, votecounter_3__10s, votecounter_3__1s}),
    .com__1({votecounter_5__1000s, votecounter_5__100s, votecounter_5__10s, votecounter_5__1s}),
    .votes__done(Votes__done), .winner(votecomparator_4_winner));
  VoteComparator votecomparator_5 (
    .main({votecounter_5__1000s, votecounter_5__100s, votecounter_5__10s, votecounter_5__1s}),
    .com__2(votecounter_1__1s),
    .com__3({votecounter_2__1000s, votecounter_2__100s, votecounter_2__10s, votecounter_2__1s}),
    .com__4({votecounter_4__1000s, votecounter_4__100s, votecounter_4__10s, votecounter_4__1s}),
    .com__1({votecounter_3__1000s, votecounter_3__100s, votecounter_3__10s, votecounter_3__1s}),
    .votes__done(Votes__done), .winner(votecomparator_5_winner));
  EEPROMDualPort #(.AddrBits(3), .isProgramMemory("true"), .Bits(16)) eepromdualport_1 (
    .A(Select), .Din({THOUSANDS_dino, HUNDREDS_dino, TENS_dino, ONES_dino}), .str(Votes__done), .C(clk),
    .ld(1'b1), .D(eepromdualport_1_d));
  LED led_2 (.in(votecomparator_1_winner));
  LED led_3 (.in(votecomparator_2_winner));
  LED led_4 (.in(votecomparator_3_winner));
  LED led_5 (.in(votecomparator_4_winner));
  LED led_6 (.in(votecomparator_5_winner));
  Seven_Seg_Hex seven_seg_hex_5 (.d(eepromdualport_1_d[15:12]), .dp(1'b0));
  Seven_Seg_Hex seven_seg_hex_6 (.d(eepromdualport_1_d[11:8]), .dp(1'b0));
  Seven_Seg_Hex seven_seg_hex_7 (.d(eepromdualport_1_d[7:4]), .dp(1'b0));
  Seven_Seg_Hex seven_seg_hex_8 (.d(eepromdualport_1_d[3:0]), .dp(1'b0));

  // Notes on the sheet:
  //   clk: Hz: 2
  //   1^st Candidate →
  //   2^nd Candidate →
  //   3^rd Candidate →
  //   4^th Candidate →
  //   5^th Candidate →
  //   Next Voter →
  //   Votes Done
  //   ↓
  //   Live Vote Counter →
  //   Vote Indicator →
  //   Result Counter →
  //   contents of eepromdualport_1 (hex, n*v repeats v):
  //   15,1,2,3,4,5
  //   WINNER
  //   0 - Total Votes
  //   1 - 1^st candidate's votes
  //   2 - 2^nd candidate's votes
  //   3 - 3^rd candidate's votes
  //   4 - 4^th candidate's votes
  //   5 - 5^th candidate's votes
  //   ← 1^st Candidate
  //   ← 2^nd Candidate
  //   ← 3^rd Candidate
  //   ← 4^th Candidate
  //   ← 5^th Candidate
endmodule
